// Logisim project alu.circ as structural Verilog: 1 circuit, main circuit alu
module alu (
  input  [31:0] A,
  input  [31:0] B,
  input  [3:0] ALUSel,
  output [31:0] Result
);

  wire bitselector_1_out, bitselector_2_out, comparator_1_eq, comparator_2_lt, comparator_3_eq;
  wire [4:0] bitselector_3_out, bitselector_4_out, bitselector_5_out;
  wire [31:0] A_BHi, ACount, add_fab51f6b, adder_3_out, adder_6_out, adder_7_out, adder_8_out, adder_9_out,
       adder_10_out, adder_11_out, adder_12_out, adder_13_out, adder_14_out, adder_15_out, adder_16_out,
       adder_17_out, adder_18_out, adder_19_out, adder_20_out, adder_21_out, adder_22_out, adder_23_out,
       adder_24_out, adder_25_out, adder_26_out, adder_27_out, adder_28_out, adder_29_out, adder_30_out,
       adder_31_out, adder_32_out, adder_33_out, adder_34_out, adder_35_out, adder_36_out, adder_37_out,
       adder_38_out, adder_39_out, adder_40_out, adder_41_out, adder_42_out, adder_43_out, adder_44_out,
       adder_45_out, adder_46_out, adder_47_out, adder_48_out, adder_49_out, adder_50_out, adder_51_out,
       adder_52_out, adder_53_out, adder_54_out, adder_55_out, adder_56_out, adder_57_out, adder_58_out,
       adder_59_out, adder_60_out, adder_61_out, adder_62_out, adder_63_out, adder_64_out, adder_65_out, AHi,
       AHi_B, and_db780d81, BCount, BHi, bit_extender_5_out, bit_extender_6_out, bit_extender_7_out,
       bit_extender_8_out, bit_extender_9_out, bit_extender_10_out, bit_extender_11_out, bit_extender_12_out,
       bit_extender_13_out, bit_extender_14_out, bit_extender_15_out, bit_extender_16_out,
       bit_extender_17_out, bit_extender_18_out, bit_extender_19_out, bit_extender_20_out,
       bit_extender_21_out, bit_extender_22_out, bit_extender_23_out, bit_extender_24_out,
       bit_extender_25_out, bit_extender_26_out, bit_extender_27_out, bit_extender_28_out,
       bit_extender_29_out, bit_extender_30_out, bit_extender_31_out, bit_extender_32_out,
       bit_extender_33_out, bit_extender_34_out, bit_extender_35_out, bit_extender_36_out,
       bit_extender_37_out, bit_extender_38_out, bit_extender_39_out, bit_extender_40_out,
       bit_extender_41_out, bit_extender_42_out, bit_extender_43_out, bit_extender_44_out,
       bit_extender_45_out, bit_extender_46_out, bit_extender_47_out, bit_extender_48_out,
       bit_extender_49_out, bit_extender_50_out, bit_extender_51_out, bit_extender_52_out,
       bit_extender_53_out, bit_extender_54_out, bit_extender_55_out, bit_extender_56_out,
       bit_extender_57_out, bit_extender_58_out, bit_extender_59_out, bit_extender_60_out,
       bit_extender_61_out, bit_extender_62_out, bit_extender_63_out, bit_extender_64_out,
       bit_extender_65_out, bit_extender_66_out, bit_extender_67_out, bit_extender_68_out, cnto_e0006c7a,
       divider_1_rem, divu_41f6ec7e, mulh_ed260fef, mulhu_ec33a2ed, mult_e521bed0, not_1_out, or_fca97519,
       remu_4c5edd16, sir_8b6db270, sll_169376c0, slt_24ef20f1, sra_1a7d4865, srl_88d3d6e3, sub_a1f6e4fd,
       xor_09867a80;

  assign not_1_out = ~B;  // NOT_Gate not_1, 32 bits wide
  BitSelector #(.width(32)) bitselector_1 (.in(A), .out(bitselector_1_out), .sel({5{1'b1}}));
  BitSelector #(.width(32)) bitselector_2 (.in(B), .out(bitselector_2_out), .sel({5{1'b1}}));
  assign and_db780d81 = A & B;  // AND_Gate and_1, 32 bits wide
  assign or_fca97519 = A | B;  // OR_Gate or_1, 32 bits wide
  assign xor_09867a80 = A ^ B;  // XOR_Gate xor_1, 32 bits wide
  Adder #(.width(32)) adder_1 (.a(A), .b(B), .out(add_fab51f6b));  // open: cin, cout
  Adder #(.width(32)) adder_2 (.a(A), .b(not_1_out), .out(sub_a1f6e4fd), .cin(1'b1));  // open: cout
  Multiplier #(.width(32)) multiplier_1 (.a(A), .b(B), .out(mult_e521bed0), .cout(mulhu_ec33a2ed));  // open: cin
  Divider #(.width(32)) divider_1 (.a(A), .b(B), .out(divu_41f6ec7e), .rem(divider_1_rem));  // open: upper
  assign AHi = {{31{bitselector_1_out}}, bitselector_1_out};  // Bit_Extender bit_extender_1
  assign BHi = {{31{bitselector_2_out}}, bitselector_2_out};  // Bit_Extender bit_extender_2
  Multiplier #(.width(32)) multiplier_2 (.a(AHi), .b(B), .out(AHi_B));  // open: cin, cout
  Multiplier #(.width(32)) multiplier_3 (.a(A), .b(BHi), .out(A_BHi));  // open: cin, cout
  Comparator #(.width(32)) comparator_1 (.a({32{1'b0}}), .b(B), .eq(comparator_1_eq));  // open: gt, lt
  Multiplexer #(.width(32), .enable("false")) multiplexer_1 (
    .in0(divider_1_rem), .in1(A), .out(remu_4c5edd16), .sel(comparator_1_eq));
  Adder #(.width(32)) adder_3 (.a(AHi_B), .b(A_BHi), .out(adder_3_out));  // open: cin, cout
  BitSelector #(.width(32), .group(5)) bitselector_3 (.in(B), .out(bitselector_3_out), .sel(3'b000));
  BitSelector #(.width(32), .group(5)) bitselector_4 (.in(B), .out(bitselector_4_out), .sel(3'b000));
  BitSelector #(.width(32), .group(5)) bitselector_5 (.in(B), .out(bitselector_5_out), .sel(3'b000));
  Adder #(.width(32)) adder_4 (.a(adder_3_out), .b(mulhu_ec33a2ed), .out(mulh_ed260fef));  // open: cin, cout
  Shifter #(.width(32), .shift("lr")) shifter_1 (.in(A), .\dist (bitselector_3_out), .out(srl_88d3d6e3));
  Shifter #(.width(32), .shift("ar")) shifter_2 (.in(A), .\dist (bitselector_4_out), .out(sra_1a7d4865));
  Shifter #(.width(32)) shifter_3 (.in(A), .\dist (bitselector_5_out), .out(sll_169376c0));
  Comparator #(.width(32)) comparator_2 (.a(A), .b(B), .lt(comparator_2_lt));  // open: gt, eq
  assign slt_24ef20f1 = {{31{1'b0}}, comparator_2_lt};  // Bit_Extender bit_extender_3
  Multiplexer #(.select(4), .width(32), .enable("false")) multiplexer_2 (
    .in0(and_db780d81), .in1(or_fca97519), .in2(xor_09867a80), .in3(add_fab51f6b), .in4(sub_a1f6e4fd),
    .in5(mult_e521bed0), .in6(mulhu_ec33a2ed), .in7(mulh_ed260fef), .in8(divu_41f6ec7e), .in9(remu_4c5edd16),
    .in10(srl_88d3d6e3), .in11(sra_1a7d4865), .in12(sll_169376c0), .in13(slt_24ef20f1), .in14(cnto_e0006c7a),
    .in15(sir_8b6db270), .out(Result), .sel(ALUSel));
  Comparator #(.width(32)) comparator_3 (
    .a({A[0], A[1], A[2], A[3], A[4], A[5], A[6], A[7], A[8], A[9], A[10], A[11], A[12], A[13], A[14], A[15], A[16], A[17], A[18], A[19], A[20], A[21], A[22], A[23], A[24], A[25], A[26], A[27], A[28], A[29], A[30], A[31]}),
    .b(B), .eq(comparator_3_eq));  // open: gt, lt
  assign sir_8b6db270 = {{31{1'b0}}, comparator_3_eq};  // Bit_Extender bit_extender_4
  Adder #(.width(32)) adder_5 (.a(ACount), .b(BCount), .out(cnto_e0006c7a));  // open: cin, cout
  assign bit_extender_5_out = {{31{1'b0}}, A[16]};  // Bit_Extender bit_extender_5
  assign bit_extender_6_out = {{31{1'b0}}, A[17]};  // Bit_Extender bit_extender_6
  assign bit_extender_7_out = {{31{1'b0}}, A[18]};  // Bit_Extender bit_extender_7
  assign bit_extender_8_out = {{31{1'b0}}, A[19]};  // Bit_Extender bit_extender_8
  assign bit_extender_9_out = {{31{1'b0}}, A[20]};  // Bit_Extender bit_extender_9
  assign bit_extender_10_out = {{31{1'b0}}, A[21]};  // Bit_Extender bit_extender_10
  assign bit_extender_11_out = {{31{1'b0}}, A[22]};  // Bit_Extender bit_extender_11
  assign bit_extender_12_out = {{31{1'b0}}, A[23]};  // Bit_Extender bit_extender_12
  assign bit_extender_13_out = {{31{1'b0}}, A[24]};  // Bit_Extender bit_extender_13
  assign bit_extender_14_out = {{31{1'b0}}, A[25]};  // Bit_Extender bit_extender_14
  assign bit_extender_15_out = {{31{1'b0}}, A[26]};  // Bit_Extender bit_extender_15
  assign bit_extender_16_out = {{31{1'b0}}, A[27]};  // Bit_Extender bit_extender_16
  assign bit_extender_17_out = {{31{1'b0}}, A[28]};  // Bit_Extender bit_extender_17
  assign bit_extender_18_out = {{31{1'b0}}, A[29]};  // Bit_Extender bit_extender_18
  assign bit_extender_19_out = {{31{1'b0}}, A[30]};  // Bit_Extender bit_extender_19
  assign bit_extender_20_out = {{31{1'b0}}, A[31]};  // Bit_Extender bit_extender_20
  assign bit_extender_21_out = {{31{1'b0}}, A[0]};  // Bit_Extender bit_extender_21
  assign bit_extender_22_out = {{31{1'b0}}, A[1]};  // Bit_Extender bit_extender_22
  assign bit_extender_23_out = {{31{1'b0}}, A[2]};  // Bit_Extender bit_extender_23
  assign bit_extender_24_out = {{31{1'b0}}, A[3]};  // Bit_Extender bit_extender_24
  assign bit_extender_25_out = {{31{1'b0}}, A[4]};  // Bit_Extender bit_extender_25
  assign bit_extender_26_out = {{31{1'b0}}, A[5]};  // Bit_Extender bit_extender_26
  assign bit_extender_27_out = {{31{1'b0}}, A[6]};  // Bit_Extender bit_extender_27
  assign bit_extender_28_out = {{31{1'b0}}, A[7]};  // Bit_Extender bit_extender_28
  assign bit_extender_29_out = {{31{1'b0}}, A[8]};  // Bit_Extender bit_extender_29
  assign bit_extender_30_out = {{31{1'b0}}, A[9]};  // Bit_Extender bit_extender_30
  assign bit_extender_31_out = {{31{1'b0}}, A[10]};  // Bit_Extender bit_extender_31
  assign bit_extender_32_out = {{31{1'b0}}, A[11]};  // Bit_Extender bit_extender_32
  assign bit_extender_33_out = {{31{1'b0}}, A[12]};  // Bit_Extender bit_extender_33
  assign bit_extender_34_out = {{31{1'b0}}, A[13]};  // Bit_Extender bit_extender_34
  assign bit_extender_35_out = {{31{1'b0}}, A[14]};  // Bit_Extender bit_extender_35
  assign bit_extender_36_out = {{31{1'b0}}, A[15]};  // Bit_Extender bit_extender_36
  assign bit_extender_37_out = {{31{1'b0}}, B[16]};  // Bit_Extender bit_extender_37
  assign bit_extender_38_out = {{31{1'b0}}, B[17]};  // Bit_Extender bit_extender_38
  assign bit_extender_39_out = {{31{1'b0}}, B[18]};  // Bit_Extender bit_extender_39
  assign bit_extender_40_out = {{31{1'b0}}, B[19]};  // Bit_Extender bit_extender_40
  assign bit_extender_41_out = {{31{1'b0}}, B[20]};  // Bit_Extender bit_extender_41
  assign bit_extender_42_out = {{31{1'b0}}, B[21]};  // Bit_Extender bit_extender_42
  assign bit_extender_43_out = {{31{1'b0}}, B[22]};  // Bit_Extender bit_extender_43
  assign bit_extender_44_out = {{31{1'b0}}, B[23]};  // Bit_Extender bit_extender_44
  assign bit_extender_45_out = {{31{1'b0}}, B[24]};  // Bit_Extender bit_extender_45
  assign bit_extender_46_out = {{31{1'b0}}, B[25]};  // Bit_Extender bit_extender_46
  assign bit_extender_47_out = {{31{1'b0}}, B[26]};  // Bit_Extender bit_extender_47
  assign bit_extender_48_out = {{31{1'b0}}, B[27]};  // Bit_Extender bit_extender_48
  assign bit_extender_49_out = {{31{1'b0}}, B[28]};  // Bit_Extender bit_extender_49
  assign bit_extender_50_out = {{31{1'b0}}, B[29]};  // Bit_Extender bit_extender_50
  assign bit_extender_51_out = {{31{1'b0}}, B[30]};  // Bit_Extender bit_extender_51
  assign bit_extender_52_out = {{31{1'b0}}, B[31]};  // Bit_Extender bit_extender_52
  assign bit_extender_53_out = {{31{1'b0}}, B[0]};  // Bit_Extender bit_extender_53
  assign bit_extender_54_out = {{31{1'b0}}, B[1]};  // Bit_Extender bit_extender_54
  assign bit_extender_55_out = {{31{1'b0}}, B[2]};  // Bit_Extender bit_extender_55
  assign bit_extender_56_out = {{31{1'b0}}, B[3]};  // Bit_Extender bit_extender_56
  assign bit_extender_57_out = {{31{1'b0}}, B[4]};  // Bit_Extender bit_extender_57
  assign bit_extender_58_out = {{31{1'b0}}, B[5]};  // Bit_Extender bit_extender_58
  assign bit_extender_59_out = {{31{1'b0}}, B[6]};  // Bit_Extender bit_extender_59
  assign bit_extender_60_out = {{31{1'b0}}, B[7]};  // Bit_Extender bit_extender_60
  assign bit_extender_61_out = {{31{1'b0}}, B[8]};  // Bit_Extender bit_extender_61
  assign bit_extender_62_out = {{31{1'b0}}, B[9]};  // Bit_Extender bit_extender_62
  assign bit_extender_63_out = {{31{1'b0}}, B[10]};  // Bit_Extender bit_extender_63
  assign bit_extender_64_out = {{31{1'b0}}, B[11]};  // Bit_Extender bit_extender_64
  assign bit_extender_65_out = {{31{1'b0}}, B[12]};  // Bit_Extender bit_extender_65
  assign bit_extender_66_out = {{31{1'b0}}, B[13]};  // Bit_Extender bit_extender_66
  assign bit_extender_67_out = {{31{1'b0}}, B[14]};  // Bit_Extender bit_extender_67
  assign bit_extender_68_out = {{31{1'b0}}, B[15]};  // Bit_Extender bit_extender_68
  Adder #(.width(32)) adder_6 (.a(bit_extender_5_out), .b(bit_extender_6_out), .out(adder_6_out));  // open: cin, cout
  Adder #(.width(32)) adder_7 (.a(bit_extender_7_out), .b(bit_extender_8_out), .out(adder_7_out));  // open: cin, cout
  Adder #(.width(32)) adder_8 (.a(bit_extender_9_out), .b(bit_extender_10_out), .out(adder_8_out));  // open: cin, cout
  Adder #(.width(32)) adder_9 (.a(bit_extender_11_out), .b(bit_extender_12_out), .out(adder_9_out));  // open: cin, cout
  Adder #(.width(32)) adder_10 (
    .a(bit_extender_13_out), .b(bit_extender_14_out), .out(adder_10_out));  // open: cin, cout
  Adder #(.width(32)) adder_11 (
    .a(bit_extender_15_out), .b(bit_extender_16_out), .out(adder_11_out));  // open: cin, cout
  Adder #(.width(32)) adder_12 (
    .a(bit_extender_17_out), .b(bit_extender_18_out), .out(adder_12_out));  // open: cin, cout
  Adder #(.width(32)) adder_13 (
    .a(bit_extender_19_out), .b(bit_extender_20_out), .out(adder_13_out));  // open: cin, cout
  Adder #(.width(32)) adder_14 (
    .a(bit_extender_21_out), .b(bit_extender_22_out), .out(adder_14_out));  // open: cin, cout
  Adder #(.width(32)) adder_15 (
    .a(bit_extender_23_out), .b(bit_extender_24_out), .out(adder_15_out));  // open: cin, cout
  Adder #(.width(32)) adder_16 (
    .a(bit_extender_25_out), .b(bit_extender_26_out), .out(adder_16_out));  // open: cin, cout
  Adder #(.width(32)) adder_17 (
    .a(bit_extender_27_out), .b(bit_extender_28_out), .out(adder_17_out));  // open: cin, cout
  Adder #(.width(32)) adder_18 (
    .a(bit_extender_29_out), .b(bit_extender_30_out), .out(adder_18_out));  // open: cin, cout
  Adder #(.width(32)) adder_19 (
    .a(bit_extender_31_out), .b(bit_extender_32_out), .out(adder_19_out));  // open: cin, cout
  Adder #(.width(32)) adder_20 (
    .a(bit_extender_33_out), .b(bit_extender_34_out), .out(adder_20_out));  // open: cin, cout
  Adder #(.width(32)) adder_21 (
    .a(bit_extender_35_out), .b(bit_extender_36_out), .out(adder_21_out));  // open: cin, cout
  Adder #(.width(32)) adder_22 (
    .a(bit_extender_37_out), .b(bit_extender_38_out), .out(adder_22_out));  // open: cin, cout
  Adder #(.width(32)) adder_23 (
    .a(bit_extender_39_out), .b(bit_extender_40_out), .out(adder_23_out));  // open: cin, cout
  Adder #(.width(32)) adder_24 (
    .a(bit_extender_41_out), .b(bit_extender_42_out), .out(adder_24_out));  // open: cin, cout
  Adder #(.width(32)) adder_25 (
    .a(bit_extender_43_out), .b(bit_extender_44_out), .out(adder_25_out));  // open: cin, cout
  Adder #(.width(32)) adder_26 (
    .a(bit_extender_45_out), .b(bit_extender_46_out), .out(adder_26_out));  // open: cin, cout
  Adder #(.width(32)) adder_27 (
    .a(bit_extender_47_out), .b(bit_extender_48_out), .out(adder_27_out));  // open: cin, cout
  Adder #(.width(32)) adder_28 (
    .a(bit_extender_49_out), .b(bit_extender_50_out), .out(adder_28_out));  // open: cin, cout
  Adder #(.width(32)) adder_29 (
    .a(bit_extender_51_out), .b(bit_extender_52_out), .out(adder_29_out));  // open: cin, cout
  Adder #(.width(32)) adder_30 (
    .a(bit_extender_53_out), .b(bit_extender_54_out), .out(adder_30_out));  // open: cin, cout
  Adder #(.width(32)) adder_31 (
    .a(bit_extender_55_out), .b(bit_extender_56_out), .out(adder_31_out));  // open: cin, cout
  Adder #(.width(32)) adder_32 (
    .a(bit_extender_57_out), .b(bit_extender_58_out), .out(adder_32_out));  // open: cin, cout
  Adder #(.width(32)) adder_33 (
    .a(bit_extender_59_out), .b(bit_extender_60_out), .out(adder_33_out));  // open: cin, cout
  Adder #(.width(32)) adder_34 (
    .a(bit_extender_61_out), .b(bit_extender_62_out), .out(adder_34_out));  // open: cin, cout
  Adder #(.width(32)) adder_35 (
    .a(bit_extender_63_out), .b(bit_extender_64_out), .out(adder_35_out));  // open: cin, cout
  Adder #(.width(32)) adder_36 (
    .a(bit_extender_65_out), .b(bit_extender_66_out), .out(adder_36_out));  // open: cin, cout
  Adder #(.width(32)) adder_37 (
    .a(bit_extender_67_out), .b(bit_extender_68_out), .out(adder_37_out));  // open: cin, cout
  Adder #(.width(32)) adder_38 (.a(adder_6_out), .b(adder_7_out), .out(adder_38_out));  // open: cin, cout
  Adder #(.width(32)) adder_39 (.a(adder_8_out), .b(adder_9_out), .out(adder_39_out));  // open: cin, cout
  Adder #(.width(32)) adder_40 (.a(adder_10_out), .b(adder_11_out), .out(adder_40_out));  // open: cin, cout
  Adder #(.width(32)) adder_41 (.a(adder_12_out), .b(adder_13_out), .out(adder_41_out));  // open: cin, cout
  Adder #(.width(32)) adder_42 (.a(adder_14_out), .b(adder_15_out), .out(adder_42_out));  // open: cin, cout
  Adder #(.width(32)) adder_43 (.a(adder_16_out), .b(adder_17_out), .out(adder_43_out));  // open: cin, cout
  Adder #(.width(32)) adder_44 (.a(adder_18_out), .b(adder_19_out), .out(adder_44_out));  // open: cin, cout
  Adder #(.width(32)) adder_45 (.a(adder_20_out), .b(adder_21_out), .out(adder_45_out));  // open: cin, cout
  Adder #(.width(32)) adder_46 (.a(adder_22_out), .b(adder_23_out), .out(adder_46_out));  // open: cin, cout
  Adder #(.width(32)) adder_47 (.a(adder_24_out), .b(adder_25_out), .out(adder_47_out));  // open: cin, cout
  Adder #(.width(32)) adder_48 (.a(adder_26_out), .b(adder_27_out), .out(adder_48_out));  // open: cin, cout
  Adder #(.width(32)) adder_49 (.a(adder_28_out), .b(adder_29_out), .out(adder_49_out));  // open: cin, cout
  Adder #(.width(32)) adder_50 (.a(adder_30_out), .b(adder_31_out), .out(adder_50_out));  // open: cin, cout
  Adder #(.width(32)) adder_51 (.a(adder_32_out), .b(adder_33_out), .out(adder_51_out));  // open: cin, cout
  Adder #(.width(32)) adder_52 (.a(adder_34_out), .b(adder_35_out), .out(adder_52_out));  // open: cin, cout
  Adder #(.width(32)) adder_53 (.a(adder_36_out), .b(adder_37_out), .out(adder_53_out));  // open: cin, cout
  Adder #(.width(32)) adder_54 (.a(adder_38_out), .b(adder_39_out), .out(adder_54_out));  // open: cin, cout
  Adder #(.width(32)) adder_55 (.a(adder_40_out), .b(adder_41_out), .out(adder_55_out));  // open: cin, cout
  Adder #(.width(32)) adder_56 (.a(adder_42_out), .b(adder_43_out), .out(adder_56_out));  // open: cin, cout
  Adder #(.width(32)) adder_57 (.a(adder_44_out), .b(adder_45_out), .out(adder_57_out));  // open: cin, cout
  Adder #(.width(32)) adder_58 (.a(adder_46_out), .b(adder_47_out), .out(adder_58_out));  // open: cin, cout
  Adder #(.width(32)) adder_59 (.a(adder_48_out), .b(adder_49_out), .out(adder_59_out));  // open: cin, cout
  Adder #(.width(32)) adder_60 (.a(adder_50_out), .b(adder_51_out), .out(adder_60_out));  // open: cin, cout
  Adder #(.width(32)) adder_61 (.a(adder_52_out), .b(adder_53_out), .out(adder_61_out));  // open: cin, cout
  Adder #(.width(32)) adder_62 (.a(adder_54_out), .b(adder_55_out), .out(adder_62_out));  // open: cin, cout
  Adder #(.width(32)) adder_63 (.a(adder_56_out), .b(adder_57_out), .out(adder_63_out));  // open: cin, cout
  Adder #(.width(32)) adder_64 (.a(adder_58_out), .b(adder_59_out), .out(adder_64_out));  // open: cin, cout
  Adder #(.width(32)) adder_65 (.a(adder_60_out), .b(adder_61_out), .out(adder_65_out));  // open: cin, cout
  Adder #(.width(32)) adder_66 (.a(adder_62_out), .b(adder_63_out), .out(ACount));  // open: cin, cout
  Adder #(.width(32)) adder_67 (.a(adder_64_out), .b(adder_65_out), .out(BCount));  // open: cin, cout

  // Other names for the same wires on the sheet: A15_0[15:0] = A[31:16];
  //   Air[31:0] = {A[0], A[1], A[2], A[3], A[4], A[5], A[6], A[7], A[8], A[9], A[10], A[11], A[12], A[13], A[14], A[15], A[16], A[17], A[18], A[19], A[20], A[21], A[22], A[23], A[24], A[25], A[26], A[27], A[28], A[29], A[30], A[31]};
  //   A31_16[15:0] = A[15:0]; B31_16[15:0] = B[15:0]; B15_0[15:0] = B[31:16]

  // Notes on the sheet:
  //   INPUTS to your circuit
  //   DON'T CHANGE THE LOCATIONS OF THE INPUTS AND OUTPUTS!
  //   OUTPUT from your circuit
endmodule
