// Logisim project cpu.circ as structural Verilog: 1 circuit, main circuit main
module main (
  input  [31:0] INSTRUCTION,
  input  in_2,
  output [31:0] FETCH_ADDRESS,
  output [31:0] ra,
  output [31:0] sp,
  output [31:0] t0,
  output [31:0] t1,
  output [31:0] t2,
  output [31:0] s0,
  output [31:0] s1,
  output [31:0] a0
);

  wire and_1_out, Asel, auipc, BrEq, BrLT, BrUn, Bsel, comparator_10_eq, comparator_11_eq, comparator_12_eq,
       comparator_12_lt, comparator_13_eq, comparator_13_lt, I, jal, jalr, load, lui, MemRW,
       multiplexer_3_out, not_2_out, not_3_out, or_1_out, or_2_out, or_4_out, or_5_out, or_6_out, or_7_out,
       or_8_out, or_9_out, or_10_out, or_11_out, or_14_out, or_15_out, or_16_out, or_17_out, PCSel, RegWEn,
       Rt, SB;
  wire [1:0] multiplexer_1_out, WBSel;
  wire [3:0] ALUSel;
  wire [11:0] bit_extender_3_out;
  wire [19:0] bit_extender_2_out;
  wire [20:0] bit_extender_1_out, bit_extender_4_out;
  wire [31:0] adder_1_out, adder_2_out, adder_3_out, ALU_r, DataA, DataB, divider_1_out, DMEM_readdata,
       fetch_addr, Imm, INSTRUCTION_t, multiplexer_4_out, multiplexer_5_out, multiplexer_8_out,
       multiplexer_9_out, multiplexer_10_out, multiplexer_11_out, multiplexer_12_out, multiplexer_13_out,
       multiplexer_14_out, multiplexer_15_out, PCa4, WB;

  Multiplexer #(.width(2), .enable("false")) multiplexer_1 (
    .in0(2'b10), .in1(2'b01), .out(multiplexer_1_out), .sel(or_1_out));
  or or_1 (or_1_out, or_4_out, or_5_out);
  or or_2 (or_2_out, SB, auipc);
  or or_3 (Asel, or_2_out, jal);
  ROM #(.addrWidth(5), .dataWidth(4)) ALU_ROM (
    .addr({INSTRUCTION_t[30], INSTRUCTION_t[25], INSTRUCTION_t[14:12]}), .data(ALUSel));
  or or_4 (or_4_out, Rt, I);
  or or_5 (or_5_out, auipc, lui);
  Multiplexer #(.width(2), .enable("false")) multiplexer_2 (
    .in0(multiplexer_1_out), .in1(2'b00), .out(WBSel), .sel(load));
  not not_1 (Bsel, Rt);
  Comparator #(.width(7)) comparator_1 (.a(7'b0110011), .b(INSTRUCTION_t[6:0]), .eq(Rt));  // open: gt, lt
  Comparator #(.width(7)) comparator_2 (.a(7'b0000011), .b(INSTRUCTION_t[6:0]), .eq(load));  // open: gt, lt
  Comparator #(.width(7)) comparator_3 (.a(7'b0010011), .b(INSTRUCTION_t[6:0]), .eq(I));  // open: gt, lt
  Comparator #(.width(7)) comparator_4 (.a(7'b0100011), .b(INSTRUCTION_t[6:0]), .eq(MemRW));  // open: gt, lt
  Comparator #(.width(7)) comparator_5 (.a(7'b1100011), .b(INSTRUCTION_t[6:0]), .eq(SB));  // open: gt, lt
  Comparator #(.width(7)) comparator_6 (.a(7'b0010111), .b(INSTRUCTION_t[6:0]), .eq(auipc));  // open: gt, lt
  Comparator #(.width(7)) comparator_7 (.a(7'b0110111), .b(INSTRUCTION_t[6:0]), .eq(lui));  // open: gt, lt
  Comparator #(.width(7)) comparator_8 (.a(7'b1101111), .b(INSTRUCTION_t[6:0]), .eq(jal));  // open: gt, lt
  Comparator #(.width(7)) comparator_9 (.a(7'b1100111), .b(INSTRUCTION_t[6:0]), .eq(jalr));  // open: gt, lt
  not not_2 (not_2_out, BrEq);
  Multiplexer #(.select(3), .enable("false")) multiplexer_3 (
    .in0(BrEq), .in1(not_2_out), .in4(BrLT), .in6(BrLT), .in7(not_3_out), .out(multiplexer_3_out),
    .sel(INSTRUCTION_t[14:12]));  // open: in2, in3, in5
  not not_3 (not_3_out, BrLT);
  or or_6 (or_6_out, jal, jalr);
  or or_7 (or_7_out, auipc, lui);
  or or_8 (or_8_out, or_7_out, or_9_out);
  or or_9 (or_9_out, jal, jalr);
  or or_10 (or_10_out, Rt, load);
  or or_11 (or_11_out, or_10_out, I);
  Comparator #(.width(3)) comparator_10 (.a(INSTRUCTION_t[14:12]), .b(3'b111), .eq(comparator_10_eq));  // open: gt, lt
  Comparator #(.width(3)) comparator_11 (.a(INSTRUCTION_t[14:12]), .b(3'b110), .eq(comparator_11_eq));  // open: gt, lt
  and and_1 (and_1_out, SB, multiplexer_3_out);
  or or_12 (RegWEn, or_8_out, or_11_out);
  or or_13 (BrUn, comparator_10_eq, comparator_11_eq);
  or or_14 (or_14_out, and_1_out, or_6_out);
  not not_4 (PCSel, or_14_out);
  // Probe on WB
  // Probe on DataA
  // Probe on Imm
  Multiplexer #(.width(32), .enable("false")) multiplexer_4 (
    .in0(DataA), .in1(fetch_addr), .out(multiplexer_4_out), .sel(Asel));
  Multiplexer #(.width(32), .enable("false")) multiplexer_5 (
    .in0(DataB), .in1(Imm), .out(multiplexer_5_out), .sel(Bsel));
  Register #(.width(32)) register_1 (.D(FETCH_ADDRESS), .en(1'b1), .clk(in_2), .Q(fetch_addr));  // open: clr
  Comparator #(.width(32)) comparator_12 (
    .a(DataA), .b(DataB), .eq(comparator_12_eq), .lt(comparator_12_lt));  // open: gt
  Multiplexer #(.enable("false")) multiplexer_6 (
    .in0(comparator_12_eq), .in1(comparator_13_eq), .out(BrEq), .sel(BrUn));
  Comparator #(.width(32), .mode("unsigned")) comparator_13 (
    .a(DataA), .b(DataB), .eq(comparator_13_eq), .lt(comparator_13_lt));  // open: gt
  Multiplexer #(.enable("false")) multiplexer_7 (
    .in0(comparator_12_lt), .in1(comparator_13_lt), .out(BrLT), .sel(BrUn));
  assign bit_extender_1_out = {{20{INSTRUCTION_t[31]}}, INSTRUCTION_t[31]};  // Bit_Extender bit_extender_1
  assign bit_extender_2_out = {{19{INSTRUCTION_t[31]}}, INSTRUCTION_t[31]};  // Bit_Extender bit_extender_2
  assign bit_extender_3_out = {{11{INSTRUCTION_t[31]}}, INSTRUCTION_t[31]};  // Bit_Extender bit_extender_3
  Multiplexer #(.width(32), .enable("false")) multiplexer_8 (
    .in0(32'h13), .in1(INSTRUCTION), .out(multiplexer_8_out), .sel(PCSel));
  regfile_main RegFile (
    .rs2(INSTRUCTION_t[24:20]), .rd(INSTRUCTION_t[11:7]), .Read_Data_1(DataA), .Read_Data_2(DataB), .ra(ra),
    .sp(sp), .t0(t0), .t1(t1), .t2(t2), .s0(s0), .s1(s1), .a0(a0), .rs1(INSTRUCTION_t[19:15]),
    .Write_Data(WB), .RegWEn(RegWEn), .clk(in_2));
  alu Arithmetic_Logic_Unit (.A(multiplexer_4_out), .B(multiplexer_5_out), .ALUSel(ALUSel), .Result(ALU_r));
  assign bit_extender_4_out = {{20{INSTRUCTION_t[31]}}, INSTRUCTION_t[31]};  // Bit_Extender bit_extender_4
  Register #(.width(32)) register_2 (.D(multiplexer_8_out), .en(1'b1), .clk(in_2), .Q(INSTRUCTION_t));  // open: clr
  // Probe on fetch_addr
  or or_15 (or_15_out, or_17_out, I);
  // Probe on {bit_extender_4_out, INSTRUCTION_t[30:20]}
  // Probe on {bit_extender_1_out, INSTRUCTION_t[30:25], INSTRUCTION_t[11:7]}
  // Probe on {bit_extender_2_out, INSTRUCTION_t[7], INSTRUCTION_t[30:25], INSTRUCTION_t[11:8], 1'b0}
  or or_16 (or_16_out, auipc, lui);
  // Probe on {INSTRUCTION_t[31:12], {12{1'b0}}}
  // Probe on {bit_extender_3_out, INSTRUCTION_t[19:12], INSTRUCTION_t[20], INSTRUCTION_t[30:21], 1'b0}
  // Probe on ALU_r
  Divider #(.width(32)) divider_1 (.a(ALU_r), .b(32'h4), .out(divider_1_out));  // open: upper, rem
  Multiplexer #(.width(32), .enable("false")) multiplexer_9 (
    .in0({32{1'b0}}), .in1({bit_extender_4_out, INSTRUCTION_t[30:20]}), .out(multiplexer_9_out),
    .sel(or_15_out));
  Multiplexer #(.width(32), .enable("false")) multiplexer_10 (
    .in0({32{1'b0}}), .in1({bit_extender_1_out, INSTRUCTION_t[30:25], INSTRUCTION_t[11:7]}),
    .out(multiplexer_10_out), .sel(MemRW));
  Multiplexer #(.width(32), .enable("false")) multiplexer_11 (
    .in0({32{1'b0}}),
    .in1({bit_extender_2_out, INSTRUCTION_t[7], INSTRUCTION_t[30:25], INSTRUCTION_t[11:8], 1'b0}),
    .out(multiplexer_11_out), .sel(SB));
  Multiplexer #(.width(32), .enable("false")) multiplexer_12 (
    .in0({32{1'b0}}), .in1({INSTRUCTION_t[31:12], {12{1'b0}}}), .out(multiplexer_12_out), .sel(or_16_out));
  Multiplexer #(.width(32), .enable("false")) multiplexer_13 (
    .in0({32{1'b0}}),
    .in1({bit_extender_3_out, INSTRUCTION_t[19:12], INSTRUCTION_t[20], INSTRUCTION_t[30:21], 1'b0}),
    .out(multiplexer_13_out), .sel(jal));
  Multiplexer #(.width(32), .enable("false")) multiplexer_14 (
    .in0(divider_1_out), .in1(PCa4), .out(multiplexer_14_out), .sel(PCSel));
  or or_17 (or_17_out, load, jalr);
  Adder #(.width(32)) adder_1 (.a(multiplexer_9_out), .b(multiplexer_10_out), .out(adder_1_out));  // open: cin, cout
  Adder #(.width(32)) adder_2 (.a(multiplexer_11_out), .b(multiplexer_12_out), .out(adder_2_out));  // open: cin, cout
  Register #(.width(32)) PC (.D(multiplexer_14_out), .en(1'b1), .clk(in_2), .Q(FETCH_ADDRESS));  // open: clr
  Adder #(.width(32)) adder_3 (.a(adder_1_out), .b(adder_2_out), .out(adder_3_out));  // open: cin, cout
  mem_main DMEM (.WriteAddr(ALU_r), .WriteData(DataB), .MemRW(MemRW), .clk(in_2), .ReadData(DMEM_readdata));
  Adder #(.width(32)) adder_4 (.a(adder_3_out), .b(multiplexer_13_out), .out(Imm));  // open: cin, cout
  Adder #(.width(32)) adder_5 (.a(32'h1), .b(FETCH_ADDRESS), .out(PCa4));  // open: cin, cout
  Multiplexer #(.select(2), .width(32), .enable("false")) multiplexer_15 (
    .in0(DMEM_readdata), .in1(ALU_r), .in2(PCa4), .out(multiplexer_15_out), .sel(WBSel));  // open: in3
  Multiplexer #(.width(32), .enable("false")) multiplexer_16 (.in0(multiplexer_15_out), .in1(Imm), .out(WB), .sel(lui));

  // Other names for the same wires on the sheet: n12_14[2:0] = INSTRUCTION_t[14:12];
  //   n15_19[4:0] = INSTRUCTION_t[19:15]; n20 = INSTRUCTION_t[20]; n21_24[3:0] = INSTRUCTION_t[24:21];
  //   n25_30[5:0] = INSTRUCTION_t[30:25]; n8_11[3:0] = INSTRUCTION_t[11:8]; n7 = INSTRUCTION_t[7];
  //   n31 = INSTRUCTION_t[31]; clk = in_2; fetch_addr_b[31:0] = FETCH_ADDRESS; INSTRUCTION_b[31:0] = INSTRUCTION;
  //   n0_6[6:0] = INSTRUCTION_t[6:0]; S = MemRW

  // Notes on the sheet:
  //   separate the instruction
  //   ASel
  //   contents of ALU_ROM (hex, n*v repeats v):
  //   3 c d 0 2 a 1 0 5 7 0 6 0 8 0 9 4 4*0 b
  //   WBSel
  //   Output
  //   ALUSel
  //   Inputs/Outputs from run.circ. DO NOT MOVE THESE.
  //   Control logic
  //   BSel
  //   Inputs
  //   R
  //   Iload
  //   I
  //   S
  //   SB
  //   auipc
  //   lui
  //   jal
  //   jalr
  //   MemRW
  //   BrUn
  //   After the program has started, there is no instruction in InstReg, so nothing in PCSel, then we automatic set PCSel to 1 at 0 time to load the instruction
  //   RegWEn
  //   PCSel
  //   It is OK to move the PC, RegFile, ALU, and MEM to wherever is most convenient for you when constructing your CPU, and to delete this text
  //   ALU
  //   Branch
  //   IF pipeline
  //   Inputs/Outputs from run.circ. DO NOT MOVE THESE.
  //   Imm Gen
  //   MEM
  //   PC
  //   anchor
endmodule
