// Logisim project cpu.circ as structural Verilog: 2 circuits, main circuit main
module main (
  input  [31:0] INSTRUCTION,
  input  in_2,
  output [31:0] FETCH_ADDRESS,
  output [31:0] ra,
  output [31:0] sp,
  output [31:0] t0,
  output [31:0] t1,
  output [31:0] t2,
  output [31:0] s0,
  output [31:0] s1,
  output [31:0] a0
);

  wire Asel, BrEq, BrLt, BrUn, Bsel, comparator_1_eq, comparator_1_lt, comparator_2_eq, comparator_2_lt, lui,
       MemRW, PCSel, RegWEn;
  wire [1:0] WBSel;
  wire [3:0] ALUSel;
  wire [31:0] ALU_r, bit_extender_1_out, bit_extender_2_out, bit_extender_3_out, bit_extender_4_out, DataA,
       DataB, divider_1_out, DMEM_readdata, fetch_addr, Imm, INSTRUCTION_t, m, multiplexer_1_out,
       multiplexer_2_out, multiplexer_3_out, multiplexer_4_out, multiplexer_8_out, multiplier_1_out,
       multiplier_2_out, PCa4, WB;

  Register #(.width(32)) register_1 (.D(FETCH_ADDRESS), .en(1'b1), .clk(in_2), .Q(fetch_addr));  // open: clr
  Register #(.width(32)) register_2 (.D(multiplexer_1_out), .en(1'b1), .clk(in_2), .Q(INSTRUCTION_t));  // open: clr
  Multiplexer #(.width(32), .enable("false")) multiplexer_1 (
    .in0(32'h13), .in1(INSTRUCTION), .out(multiplexer_1_out), .sel(PCSel));
  control control_1 (
    .Imm(Imm), .INSTRUCTION(INSTRUCTION_t), .RegWEn(RegWEn), .RemRW(MemRW), .BrEq(BrEq), .PCSel(PCSel),
    .BrLt(BrLt), .WBSel(WBSel), .BSel(Bsel), .ASel(Asel), .ALUSel(ALUSel), .lui(lui), .BrUn(BrUn));
  // Probe on fetch_addr
  // Probe on INSTRUCTION_t
  // Probe on WB
  // Probe on multiplier_1_out
  Multiplier #(.width(32)) multiplier_1 (.a(fetch_addr), .b(32'h4), .out(multiplier_1_out));  // open: cin, cout
  // Probe on DataA
  // Probe on Imm
  Multiplexer #(.width(32), .enable("false")) multiplexer_2 (
    .in0(DataA), .in1(multiplier_1_out), .out(multiplexer_2_out), .sel(Asel));
  Multiplexer #(.width(32), .enable("false")) multiplexer_3 (
    .in0(DataB), .in1(Imm), .out(multiplexer_3_out), .sel(Bsel));
  Multiplier #(.width(32)) multiplier_2 (.a(32'h2), .b(PCa4), .out(multiplier_2_out));  // open: cin, cout
  Multiplexer #(.select(2), .width(32), .enable("false")) multiplexer_4 (
    .in0(m), .in1(ALU_r), .in2(multiplier_2_out), .out(multiplexer_4_out), .sel(WBSel));  // open: in3
  Comparator #(.width(32)) comparator_1 (.a(DataA), .b(DataB), .eq(comparator_1_eq), .lt(comparator_1_lt));  // open: gt
  Multiplexer #(.enable("false")) multiplexer_5 (.in0(comparator_1_eq), .in1(comparator_2_eq), .out(BrEq), .sel(BrUn));
  Comparator #(.width(32), .mode("unsigned")) comparator_2 (
    .a(DataA), .b(DataB), .eq(comparator_2_eq), .lt(comparator_2_lt));  // open: gt
  Multiplexer #(.enable("false")) multiplexer_6 (.in0(comparator_1_lt), .in1(comparator_2_lt), .out(BrLt), .sel(BrUn));
  Multiplexer #(.width(32), .enable("false")) multiplexer_7 (.in0(multiplexer_4_out), .in1(Imm), .out(WB), .sel(lui));
  regfile_main RegFile (
    .rs2(INSTRUCTION_t[24:20]), .rd(INSTRUCTION_t[11:7]), .Read_Data_1(DataA), .Read_Data_2(DataB), .ra(ra),
    .sp(sp), .t0(t0), .t1(t1), .t2(t2), .s0(s0), .s1(s1), .a0(a0), .rs1(INSTRUCTION_t[19:15]),
    .Write_Data(WB), .RegWEn(RegWEn), .clk(in_2));
  alu Arithmetic_Logic_Unit (.A(multiplexer_2_out), .B(multiplexer_3_out), .ALUSel(ALUSel), .Result(ALU_r));
  // Probe on DataB
  // Probe on DataA
  // Probe on ALU_r
  Divider #(.width(32)) divider_1 (.a(ALU_r), .b(32'h4), .out(divider_1_out));  // open: upper, rem
  Multiplexer #(.width(32), .enable("false")) multiplexer_8 (
    .in0(divider_1_out), .in1(PCa4), .out(multiplexer_8_out), .sel(PCSel));
  Register #(.width(32)) PC (.D(multiplexer_8_out), .en(1'b1), .clk(in_2), .Q(FETCH_ADDRESS));  // open: clr
  mem_main DMEM (.WriteAddr(ALU_r), .WriteData(DataB), .MemRW(MemRW), .clk(in_2), .ReadData(DMEM_readdata));
  Adder #(.width(32)) adder_1 (.a(32'h1), .b(FETCH_ADDRESS), .out(PCa4));  // open: cin, cout
  assign bit_extender_1_out = {{24{DMEM_readdata[7]}}, DMEM_readdata[7:0]};  // Bit_Extender bit_extender_1
  assign bit_extender_2_out = {{24{1'b0}}, DMEM_readdata[7:0]};  // Bit_Extender bit_extender_2
  assign bit_extender_3_out = {{16{DMEM_readdata[15]}}, DMEM_readdata[15:0]};  // Bit_Extender bit_extender_3
  assign bit_extender_4_out = {{16{1'b0}}, DMEM_readdata[15:0]};  // Bit_Extender bit_extender_4
  Multiplexer #(.select(3), .width(32), .enable("false")) multiplexer_9 (
    .in0(bit_extender_1_out), .in1(bit_extender_3_out), .in2(DMEM_readdata), .in4(bit_extender_2_out),
    .in5(bit_extender_4_out), .out(m), .sel(INSTRUCTION_t[14:12]));  // open: in3, in6, in7

  // Other names for the same wires on the sheet: clk = in_2; fetch_addr_b[31:0] = FETCH_ADDRESS;
  //   INSTRUCTION_b[31:0] = INSTRUCTION; n12_14[2:0] = INSTRUCTION_t[14:12]

  // Notes on the sheet:
  //   Output
  //   Inputs/Outputs from run.circ. DO NOT MOVE THESE.
  //   Control logic
  //   Inputs
  //   IF pipeline
  //   It is OK to move the PC, RegFile, ALU, and MEM to wherever is most convenient for you when constructing your CPU, and to delete this text
  //   WB
  //   ALU
  //   Branch
  //   Inputs/Outputs from run.circ. DO NOT MOVE THESE.
  //   MEM
  //   PC
  //   anchor
endmodule

module control (
  input  [31:0] INSTRUCTION,
  input  BrLt,
  input  BrEq,
  output [31:0] Imm,
  output RegWEn,
  output BSel,
  output ASel,
  output RemRW,
  output [1:0] WBSel,
  output PCSel,
  output [3:0] ALUSel,
  output lui,
  output BrUn
);

  wire and_1_out, auipc, comparator_1_eq, comparator_2_eq, comparator_12_eq, I, jal, jalr, load,
       multiplexer_2_out, not_1_out, not_2_out, or_1_out, or_2_out, or_3_out, or_5_out, or_6_out, or_8_out,
       or_9_out, or_10_out, or_11_out, or_12_out, or_13_out, or_15_out, or_16_out, or_17_out, or_18_out,
       or_19_out, or_20_out, or_21_out, or_22_out, Rt, SB;
  wire [1:0] multiplexer_1_out;
  wire [3:0] multiplexer_9_out, multiplexer_10_out, multiplexer_11_out, rom_1_data, rom_2_data;
  wire [19:0] bit_extender_2_out;
  wire [20:0] bit_extender_1_out, bit_extender_4_out;
  wire [31:0] adder_1_out, adder_2_out, adder_3_out, multiplexer_4_out, multiplexer_5_out, multiplexer_6_out,
       multiplexer_7_out, multiplexer_8_out;
  wire [31:20] bit_extender_3_out;

  Multiplexer #(.width(2), .enable("false")) multiplexer_1 (
    .in0(2'b10), .in1(2'b01), .out(multiplexer_1_out), .sel(or_1_out));
  or or_1 (or_1_out, or_5_out, or_6_out);
  not not_1 (not_1_out, BrEq);
  not not_2 (not_2_out, BrLt);
  or or_2 (or_2_out, jal, jalr);
  or or_3 (or_3_out, SB, auipc);
  or or_4 (ASel, or_3_out, jal);
  or or_5 (or_5_out, Rt, I);
  or or_6 (or_6_out, auipc, lui);
  Multiplexer #(.select(3), .enable("false")) multiplexer_2 (
    .in0(BrEq), .in1(not_1_out), .in4(BrLt), .in6(BrLt), .in7(not_2_out), .out(multiplexer_2_out),
    .sel(INSTRUCTION[14:12]));  // open: in2, in3, in5
  Multiplexer #(.width(2), .enable("false")) multiplexer_3 (
    .in0(multiplexer_1_out), .in1(2'b00), .out(WBSel), .sel(load));
  Comparator #(.width(3)) comparator_1 (.a(INSTRUCTION[14:12]), .b(3'b111), .eq(comparator_1_eq));  // open: gt, lt
  or or_7 (BrUn, comparator_1_eq, comparator_2_eq);
  Comparator #(.width(3)) comparator_2 (.a(INSTRUCTION[14:12]), .b(3'b110), .eq(comparator_2_eq));  // open: gt, lt
  and and_1 (and_1_out, SB, multiplexer_2_out);
  or or_8 (or_8_out, and_1_out, or_2_out);
  not not_3 (PCSel, or_8_out);
  or or_9 (or_9_out, auipc, lui);
  or or_10 (or_10_out, or_9_out, or_11_out);
  or or_11 (or_11_out, jal, jalr);
  or or_12 (or_12_out, Rt, load);
  or or_13 (or_13_out, or_12_out, I);
  not not_4 (BSel, Rt);
  Comparator #(.width(7)) comparator_3 (.a(7'b0110011), .b(INSTRUCTION[6:0]), .eq(Rt));  // open: gt, lt
  Comparator #(.width(7)) comparator_4 (.a(7'b0000011), .b(INSTRUCTION[6:0]), .eq(load));  // open: gt, lt
  Comparator #(.width(7)) comparator_5 (.a(7'b0010011), .b(INSTRUCTION[6:0]), .eq(I));  // open: gt, lt
  Comparator #(.width(7)) comparator_6 (.a(7'b0100011), .b(INSTRUCTION[6:0]), .eq(RemRW));  // open: gt, lt
  Comparator #(.width(7)) comparator_7 (.a(7'b1100011), .b(INSTRUCTION[6:0]), .eq(SB));  // open: gt, lt
  Comparator #(.width(7)) comparator_8 (.a(7'b0010111), .b(INSTRUCTION[6:0]), .eq(auipc));  // open: gt, lt
  Comparator #(.width(7)) comparator_9 (.a(7'b0110111), .b(INSTRUCTION[6:0]), .eq(lui));  // open: gt, lt
  Comparator #(.width(7)) comparator_10 (.a(7'b1101111), .b(INSTRUCTION[6:0]), .eq(jal));  // open: gt, lt
  Comparator #(.width(7)) comparator_11 (.a(7'b1100111), .b(INSTRUCTION[6:0]), .eq(jalr));  // open: gt, lt
  or or_14 (RegWEn, or_10_out, or_13_out);
  ROM #(.addrWidth(3), .dataWidth(4)) rom_1 (.addr(INSTRUCTION[14:12]), .data(rom_1_data));
  assign bit_extender_1_out = {{20{INSTRUCTION[31]}}, INSTRUCTION[31]};  // Bit_Extender bit_extender_1
  assign bit_extender_2_out = {{19{INSTRUCTION[31]}}, INSTRUCTION[31]};  // Bit_Extender bit_extender_2
  assign bit_extender_3_out = {{11{INSTRUCTION[31]}}, INSTRUCTION[31]};  // Bit_Extender bit_extender_3
  assign bit_extender_4_out = {{20{INSTRUCTION[31]}}, INSTRUCTION[31]};  // Bit_Extender bit_extender_4
  ROM #(.addrWidth(5), .dataWidth(4)) rom_2 (
    .addr({INSTRUCTION[30], INSTRUCTION[25], INSTRUCTION[14:12]}), .data(rom_2_data));
  Comparator #(.width(3)) comparator_12 (.a(INSTRUCTION[14:12]), .b(3'b101), .eq(comparator_12_eq));  // open: gt, lt
  Multiplexer #(.width(32), .enable("false")) multiplexer_4 (
    .in0({32{1'b0}}), .in1({bit_extender_4_out, INSTRUCTION[30:20]}), .out(multiplexer_4_out), .sel(or_15_out));
  or or_15 (or_15_out, or_17_out, I);
  // Probe on {bit_extender_4_out, INSTRUCTION[30:20]}
  Multiplexer #(.width(32), .enable("false")) multiplexer_5 (
    .in0({32{1'b0}}), .in1({bit_extender_1_out, INSTRUCTION[30:25], INSTRUCTION[11:7]}),
    .out(multiplexer_5_out), .sel(RemRW));
  // Probe on {bit_extender_1_out, INSTRUCTION[30:25], INSTRUCTION[11:7]}
  Multiplexer #(.width(32), .enable("false")) multiplexer_6 (
    .in0({32{1'b0}}),
    .in1({bit_extender_2_out, INSTRUCTION[7], INSTRUCTION[30:25], INSTRUCTION[11:8], 1'b0}),
    .out(multiplexer_6_out), .sel(SB));
  // Probe on {bit_extender_2_out, INSTRUCTION[7], INSTRUCTION[30:25], INSTRUCTION[11:8], 1'b0}
  Multiplexer #(.width(32), .enable("false")) multiplexer_7 (
    .in0({32{1'b0}}), .in1({INSTRUCTION[31:12], {12{1'b0}}}), .out(multiplexer_7_out), .sel(or_16_out));
  or or_16 (or_16_out, auipc, lui);
  // Probe on {INSTRUCTION[31:12], {12{1'b0}}}
  Multiplexer #(.width(32), .enable("false")) multiplexer_8 (
    .in0({32{1'b0}}),
    .in1({bit_extender_3_out, INSTRUCTION[19:12], INSTRUCTION[20], INSTRUCTION[30:21], 1'b0}),
    .out(multiplexer_8_out), .sel(jal));
  Multiplexer #(.width(4), .enable("false")) multiplexer_9 (
    .in0(4'b1010), .in1(4'b1011), .out(multiplexer_9_out), .sel(INSTRUCTION[30]));
  Multiplexer #(.width(4), .enable("false")) multiplexer_10 (
    .in0(rom_1_data), .in1(multiplexer_9_out), .out(multiplexer_10_out), .sel(comparator_12_eq));
  or or_17 (or_17_out, jalr, load);
  Adder #(.width(32)) adder_1 (.a(multiplexer_4_out), .b(multiplexer_5_out), .out(adder_1_out));  // open: cin, cout
  Adder #(.width(32)) adder_2 (.a(multiplexer_6_out), .b(multiplexer_7_out), .out(adder_2_out));  // open: cin, cout
  Multiplexer #(.width(4), .enable("false")) multiplexer_11 (
    .in0(rom_2_data), .in1(multiplexer_10_out), .out(multiplexer_11_out), .sel(I));
  Adder #(.width(32)) adder_3 (.a(adder_1_out), .b(adder_2_out), .out(adder_3_out));  // open: cin, cout
  Multiplexer #(.width(4), .enable("false")) multiplexer_12 (
    .in0(multiplexer_11_out), .in1(4'b0011), .out(ALUSel), .sel(or_18_out));
  or or_18 (or_18_out, or_19_out, or_20_out);
  Adder #(.width(32)) adder_4 (.a(adder_3_out), .b(multiplexer_8_out), .out(Imm));  // open: cin, cout
  or or_19 (or_19_out, or_22_out, RemRW);
  or or_20 (or_20_out, load, SB);
  or or_21 (or_21_out, auipc, jal);
  or or_22 (or_22_out, or_21_out, jalr);

  // Other names for the same wires on the sheet: n31 = INSTRUCTION[31]; n21_24[3:0] = INSTRUCTION[24:21];
  //   n25_30[5:0] = INSTRUCTION[30:25]; n20 = INSTRUCTION[20]; n12_14[2:0] = INSTRUCTION[14:12];
  //   n15_19[4:0] = INSTRUCTION[19:15]; n8_11[3:0] = INSTRUCTION[11:8]; n7 = INSTRUCTION[7];
  //   n0_6[6:0] = INSTRUCTION[6:0]; MemRW = RemRW; S = RemRW

  // Notes on the sheet:
  //   ASel
  //   WBSel
  //   BrUn
  //   PCSel
  //   R
  //   Iload
  //   I
  //   S
  //   SB
  //   auipc
  //   lui
  //   jal
  //   jalr
  //   RegWEn
  //   BSel
  //   MemRW
  //   contents of rom_1 (hex, n*v repeats v):
  //   3 c d 0 2 a 1
  //   Imm Gen
  //   contents of rom_2 (hex, n*v repeats v):
  //   3 c d 0 2 a 1 0 5 7 0 6 0 8 0 9 4 4*0 b
  //   ALUSel
  //   0 :reg
  //   0: mem 1: alu 2:pc+4
endmodule
