// Logisim project mem.circ as structural Verilog: 1 circuit, main circuit mem
module mem (
  input  [31:0] WriteAddr,
  input  MemRW,
  input  clk,
  input  [31:0] WriteData,
  output [31:0] ReadData
);

  RAM #(.addrWidth(24), .dataWidth(32), .databus("bibus")) DMEM (
    .addr(WriteAddr[25:2]), .we(MemRW), .oe(1'b1), .clk(clk), .din(WriteData), .dout(ReadData));
endmodule
