// Logisim project alu.circ as structural Verilog: 1 circuit, main circuit alu
module alu (
  input  [31:0] A,
  input  [31:0] B,
  input  [3:0] ALUSel,
  output [31:0] Result
);

  wire comparator_1_lt;
  wire [4:0] bitselector_1_out, bitselector_2_out, bitselector_3_out;
  wire [31:0] add_, and_, cnto_, divu_, mulh_, mulhu_, mult_, not_1_out, or_, remu_, sir_, sll_, slt_, sra_,
       srl_, sub_, xor_;

  assign not_1_out = ~B;  // NOT_Gate not_1, 32 bits wide
  assign and_ = A & B;  // AND_Gate and_1, 32 bits wide
  assign or_ = A | B;  // OR_Gate or_1, 32 bits wide
  assign xor_ = A ^ B;  // XOR_Gate xor_1, 32 bits wide
  Adder #(.width(32)) adder_1 (.a(A), .b(B), .out(add_));  // open: cin, cout
  Adder #(.width(32)) adder_2 (.a(A), .b(not_1_out), .out(sub_), .cin(1'b1));  // open: cout
  BitSelector #(.width(32), .group(5)) bitselector_1 (.in(B), .out(bitselector_1_out), .sel(3'b000));
  BitSelector #(.width(32), .group(5)) bitselector_2 (.in(B), .out(bitselector_2_out), .sel(3'b000));
  BitSelector #(.width(32), .group(5)) bitselector_3 (.in(B), .out(bitselector_3_out), .sel(3'b000));
  Shifter #(.width(32), .shift("lr")) shifter_1 (.in(A), .\dist (bitselector_1_out), .out(srl_));
  Shifter #(.width(32), .shift("ar")) shifter_2 (.in(A), .\dist (bitselector_2_out), .out(sra_));
  Shifter #(.width(32)) shifter_3 (.in(A), .\dist (bitselector_3_out), .out(sll_));
  Comparator #(.width(32)) comparator_1 (.a(A), .b(B), .lt(comparator_1_lt));  // open: gt, eq
  assign slt_ = {{31{1'b0}}, comparator_1_lt};  // Bit_Extender bit_extender_1
  Multiplexer #(.select(4), .width(32), .enable("false")) multiplexer_1 (
    .in0(and_), .in1(or_), .in2(xor_), .in3(add_), .in4(sub_), .in5(mult_), .in6(mulhu_), .in7(mulh_),
    .in8(divu_), .in9(remu_), .in10(srl_), .in11(sra_), .in12(sll_), .in13(slt_), .in14(cnto_), .in15(sir_),
    .out(Result), .sel(ALUSel));

  // Notes on the sheet:
  //   INPUTS to your circuit
  //   DON'T CHANGE THE LOCATIONS OF THE INPUTS AND OUTPUTS!
  //   OUTPUT from your circuit
endmodule
