// Logisim project mem.circ as structural Verilog: 1 circuit, main circuit main
module main (
  input  [31:0] WriteAddr,
  input  [31:0] ReadData,
  input  [31:0] WriteData,
  input  MemRW,
  input  clk
);

  RAM #(.addrWidth(24), .dataWidth(32), .databus("bibus")) DMEM (
    .addr(WriteData[23:0]), .we(MemRW), .oe(1'b1), .clk(clk), .din(WriteAddr), .dout(ReadData));

  // Notes on the sheet:
  //   DMEM
endmodule
