// Logisim project regfile.circ as structural Verilog: 1 circuit, main circuit main
module main (
  input  [4:0] rs1,
  input  [4:0] rs2,
  input  [4:0] rd,
  input  [31:0] Write_Data,
  input  RegWEn,
  input  clk,
  output [31:0] ra,
  output [31:0] sp,
  output [31:0] t0,
  output [31:0] t1,
  output [31:0] t2,
  output [31:0] s0,
  output [31:0] s1,
  output [31:0] a0,
  output [31:0] Read_Data_1,
  output [31:0] Read_Data_2
);

  wire en1, en2, en5, en6, en7, en8, en9, ena;
  wire [31:0] x1, x2, x5, x6, x7, x8, x9, xa;

  Register #(.width(32)) register_1 (.D(Write_Data), .en(en1), .clk(clk), .Q(x1));  // open: clr
  Register #(.width(32)) register_2 (.D(Write_Data), .en(en2), .clk(clk), .Q(x2));  // open: clr
  Register #(.width(32)) register_3 (.D(Write_Data), .en(en5), .clk(clk), .Q(x5));  // open: clr
  Register #(.width(32)) register_4 (.D(Write_Data), .en(en6), .clk(clk), .Q(x6));  // open: clr
  Register #(.width(32)) register_5 (.D(Write_Data), .en(en7), .clk(clk), .Q(x7));  // open: clr
  Register #(.width(32)) register_6 (.D(Write_Data), .en(en8), .clk(clk), .Q(x8));  // open: clr
  Register #(.width(32)) register_7 (.D(Write_Data), .en(en9), .clk(clk), .Q(x9));  // open: clr
  Register #(.width(32)) register_8 (.D(Write_Data), .en(ena), .clk(clk), .Q(xa));  // open: clr
  Multiplexer #(.select(5), .width(32), .enable("false")) multiplexer_1 (
    .in0({32{1'b0}}), .in1(x1), .in2(x2), .in5(x5), .in6(x6), .in7(x7), .in8(x8), .in9(x9), .in10(xa),
    .out(Read_Data_2), .sel(rs2));  // open: in3, in4, in11, in12, in13, in14, in15, in16, in17, in18, in19, in20, in21, in22, in23, in24, in25, in26, in27, in28, in29, in30, in31
  Multiplexer #(.select(5), .width(32), .enable("false")) multiplexer_2 (
    .in0({32{1'b0}}), .in1(x1), .in2(x2), .in5(x5), .in6(x6), .in7(x7), .in8(x8), .in9(x9), .in10(xa),
    .out(Read_Data_1), .sel(rs1));  // open: in3, in4, in11, in12, in13, in14, in15, in16, in17, in18, in19, in20, in21, in22, in23, in24, in25, in26, in27, in28, in29, in30, in31

  // Other names for the same wires on the sheet: read_data1[31:0] = Read_Data_1; read_data2[31:0] = Read_Data_2;
  //   read_reg1[4:0] = rs1; read_reg2[4:0] = rs2; write_en = RegWEn; write_reg[4:0] = rd

  // Notes on the sheet:
  //   INPUTS to your circuit
  //   DON'T CHANGE THE LOCATIONS OF THE INPUTS AND OUTPUTS!
  //   These are DEBUG/TEST outputs from your circuit.
  //   OUTPUTS from your circuit
endmodule
